// Logisim project bonkpu.circ as structural Verilog: 4 circuits, main circuit main
module main (
);

  wire AI, and_1_out, and_2_out, AO, BI, BO, button_1_out, CE, CHI, CHO, CLI, CLK, CLO, clock_1_out,
       comparator_1_eq, dipswitch_1_p1, EO, FI, HLT, IE, II, MB, MHI, MLI, MU, nor_2_out, not_1_out,
       not_2_out, RI, RO, SHO, SLO, SU, xor_2_out;
  wire [1:0] STACK_MODE;
  wire [2:0] FLAGS, nor_1_out;
  wire [3:0] MICROSTEP_q;
  wire [7:0] A_REG_q, adder_2_out, B_REG_q, MEM_dout, microcode_c_data, multiplexer_2_out, OP_REG_q,
       PROGMEM_data, stack_pointer_1_out_bus, xor_1_out;
  wire [14:0] adder_1_out;
  wire [15:0] mar_1_addr;
  wire [15:15] adder_1_out_2;

  ROM #(.addrWidth(15)) PROGMEM (.addr(adder_1_out), .data(PROGMEM_data));
  Counter #(.max('hf), .width(4)) MICROSTEP (
    .load(IE), .clk(not_1_out), .D(4'b0000), .Q(MICROSTEP_q));  // open: clr, up, count, carry
  not not_1 (not_1_out, CLK);
  Register OP_REG (.D(stack_pointer_1_out_bus), .en(II), .clk(CLK), .Q(OP_REG_q));  // open: clr
  stack_pointer stack_pointer_1 (.HO(SHO), .LO(SLO), .CLK(CLK), .MODE(STACK_MODE), .out_bus(stack_pointer_1_out_bus));
  program_counter program_counter_1 (
    .CLK(CLK), .CE(CE), .LI(CLI), .HI(CHI), .HO(CHO), .LO(CLO), .bus_in(stack_pointer_1_out_bus),
    .bus_out(stack_pointer_1_out_bus));
  mar mar_1 (.CLK(CLK), .HI(MHI), .LI(MLI), .bus_in(stack_pointer_1_out_bus), .U(MU), .addr(mar_1_addr));
  and and_1 (and_1_out, adder_1_out_2[15], RI);
  RAM #(.addrWidth(15), .enables("line")) MEM (
    .addr(adder_1_out), .we(and_1_out), .clk(CLK), .din(stack_pointer_1_out_bus), .dout(MEM_dout));
  Adder #(.width(16)) adder_1 (
    .a({16{1'b0}}), .b(mar_1_addr), .out({adder_1_out_2[15], adder_1_out}), .cin(MB));  // open: cout
  ROM #(.addrWidth(15)) microcode_a (.addr({FLAGS, OP_REG_q, MICROSTEP_q}), .data({HLT, MHI, MLI, RI, MU, MB, II, AI}));
  Multiplexer #(.disabled("Z"), .enable("true"), .width(8)) multiplexer_1 (
    .in0(PROGMEM_data), .in1(MEM_dout), .out(stack_pointer_1_out_bus), .sel(adder_1_out_2[15]), .en(RO));
  LedBar ledbar_1 (
    .led0(stack_pointer_1_out_bus[7]), .led1(stack_pointer_1_out_bus[6]), .led2(stack_pointer_1_out_bus[5]),
    .led3(stack_pointer_1_out_bus[4]), .led4(stack_pointer_1_out_bus[3]), .led5(stack_pointer_1_out_bus[2]),
    .led6(stack_pointer_1_out_bus[1]), .led7(stack_pointer_1_out_bus[0]));
  Pull_Resistor pull_resistor_1 (.node(stack_pointer_1_out_bus));
  ROM #(.addrWidth(15)) microcode_b (
    .addr({FLAGS, OP_REG_q, MICROSTEP_q}), .data({BI, SU, FI, CE, CHI, CLI, STACK_MODE}));
  assign stack_pointer_1_out_bus = EO ? adder_2_out : 8'bz;  // Controlled_Buffer EO_GATE
  Register A_REG (.D(stack_pointer_1_out_bus), .en(AI), .clk(CLK), .Q(A_REG_q));  // open: clr
  assign stack_pointer_1_out_bus = AO ? A_REG_q : 8'bz;  // Controlled_Buffer controlled_buffer_1
  Register B_REG (.D(stack_pointer_1_out_bus), .en(BI), .clk(CLK), .Q(B_REG_q));  // open: clr
  assign stack_pointer_1_out_bus = BO ? B_REG_q : 8'bz;  // Controlled_Buffer B_GATE
  Multiplexer #(.width(8)) multiplexer_2 (.in0({8{1'b0}}), .in1({8{1'b1}}), .out(multiplexer_2_out), .sel(SU));
  ROM #(.addrWidth(15)) microcode_c (
    .addr({FLAGS, OP_REG_q, MICROSTEP_q}), .data({microcode_c_data[7:5], IE, microcode_c_data[3:0]}));
  LedBar #(.matrixcols(24)) ledbar_2 (
    .led0(HLT), .led1(MHI), .led2(MLI), .led3(RI), .led4(MU), .led5(MB), .led6(II), .led7(AI), .led8(BI),
    .led9(SU), .led10(FI), .led11(CE), .led12(CHI), .led13(CLI), .led14(STACK_MODE[1]),
    .led15(STACK_MODE[0]), .led16(microcode_c_data[7]), .led17(microcode_c_data[6]),
    .led18(microcode_c_data[5]), .led19(IE), .led20(microcode_c_data[3]), .led21(microcode_c_data[2]),
    .led22(microcode_c_data[1]), .led23(microcode_c_data[0]));
  assign xor_1_out = multiplexer_2_out ^ B_REG_q;  // XOR_Gate xor_1, 8 bits wide
  // Probe on B_REG_q
  // Probe on B_REG_q
  // Probe on A_REG_q
  // Probe on A_REG_q
  Adder adder_2 (.a(A_REG_q), .b(xor_1_out), .out(adder_2_out), .cin(SU), .cout(nor_1_out[2]));
  // Probe on adder_2_out
  // Probe on adder_2_out
  nor nor_1 (nor_1_out[0], adder_2_out[0], adder_2_out[1], adder_2_out[2], adder_2_out[3], adder_2_out[4], adder_2_out[5], adder_2_out[6], adder_2_out[7]);
  Clock clock_1 (.out(clock_1_out));
  Comparator #(.mode("unsigned"), .width(4)) comparator_1 (
    .a(MICROSTEP_q), .b(4'b0000), .eq(comparator_1_eq));  // open: gt, lt
  Register #(.width(3)) FLAG_REG (
    .D({nor_1_out[2], adder_2_out[7], nor_1_out[0]}), .en(FI), .clk(CLK), .Q(FLAGS));  // open: clr
  nor nor_2 (nor_2_out, HLT, and_2_out);
  and and_2 (and_2_out, comparator_1_eq, xor_2_out);
  LedBar #(.matrixcols(3)) ledbar_3 (.led0(FLAGS[2]), .led1(FLAGS[1]), .led2(FLAGS[0]));
  Decoder #(.enable("false"), .select(4)) decoder_1 (
    .out1(RO), .out2(AO), .out3(BO), .out4(EO), .out5(CHO), .out6(CLO), .out7(SHO), .out8(SLO),
    .sel(microcode_c_data[3:0]));  // open: out0, out9, out10, out11, out12, out13, out14, out15
  and and_3 (CLK, clock_1_out, nor_2_out);
  xor xor_2 (xor_2_out, button_1_out, not_2_out);
  not not_2 (not_2_out, dipswitch_1_p1);
  Button #(.press("passive")) button_1 (.out(button_1_out));
  // DipSwitch #(.number(2)) dipswitch_1: pin names not known; wires that end beside it: dipswitch_1_p1

  // Notes on the sheet:
  //   contents of PROGMEM (hex, n*v repeats v):
  //   11 1 4 4 0 80 1 6 4 1 80 16 1a 0 4 0 80 1 9 4 1 80 16 1a 0 18 2 0 80 9 1 80 10 35 0 2 0 80 4 2 80 2
  //   1 80 4 0 80 2 2 80 4 1 80 2 0 80 4 2 80 1 0 4 3 80 2 3 80 7 1 80 4 3 80 2 2 80 8 1 4 2 80 c 40 0 2 3
  //   80 17
  //   contents of microcode_a (hex, n*v repeats v):
  //   20 48 2 13*0 20 48 2 20 48 1 10*0 20 48 2 20 48 20 4c 1 8*0 20 48 2 20 48 20 4c 20 4c 1 6*0 20 48 2
  //   20 48 20 4c 10 8*0 20 48 2 20 48 20 4c 20 4c 10 6*0 20 48 2 20 48 0 1 9*0 20 48 2 20 48 20 4c 0 1
  //   7*0 20 48 2 20 48 0 1 9*0 20 48 2 20 48 20 4c 0 1 7*0 20 48 2 20 48 0 4 9*0 20 48 2 13*0 20 48 2 20
  //   48 0 4 9*0 20 48 2 13*0 20 48 2 20 48 0 4 9*0 20 48 2 13*0 20 48 2 20 48 0 4 9*0 20 48 2 13*0 20 48
  //   2 13*0 20 48 2 13*0 20 48 2 20 48 10 10*0 20 48 2 0 20 48 1 9*0 20 48 2 20 48 10 20 48 10 20 48 0 4
  //   0 0 0 20 48 2 0 20 48 0 20 48 7*0 20 48 2 80 12*0 20 48 2 13*0 20 48 2 13*0 20 48 2 13*0 20 48 2
  //   13*0 20 48 2 13*0 20 48 2 13*0 20 48 2 13*0 20 48 2 13*0 20 48 2 13*0 20 48 2 13*0 20 48 2 13*0 20
  //   48 2 13*0 20 48 2 13*0 20 48 2 13*0 20 48 2 13*0 20 48 2 13*0 20 48 2 13*0 20 48 2 13*0 20 48 2 13*0
  //   20 48 2 13*0 20 48 2 13*0 20 48 2 13*0 20 48 2 13*0 20 48 2 13*0 20 48 2 13*0 20 48 2 13*0 20 48 2
  //   13*0 20 48 2 13*0 20 48 2 13*0 20 48 2 13*0 20 48 2 13*0 20 48 2 13*0 20 48 2 13*0 20 48 2 13*0 20
  //   48 2 13*0 20 48 2 13*0 20 48 2 13*0 20 48 2 13*0 20 48 2 13*0 20 48 2 13*0 20 48 2 13*0 20 48 2 13*0
  //   20 48 2 13*0 20 48 2 13*0 20 48 2 13*0 20 48 2 13*0 20 48 2 13*0 20 48 2 13*0 20 48 2 13*0 20 48 2
  //   13*0 20 48 2 13*0 20 48 2 13*0 20 48 2 13*0 20 48 2 13*0 20 48 2 13*0 20 48 2 13*0 20 48 2 13*0 20
  //   48 2 13*0 20 48 2 13*0 20 48 2 13*0 20 48 2 13*0 20 48 2 13*0 20 48 2 13*0 20 48 2 13*0 20 48 2 13*0
  //   20 48 2 13*0 20 48 2 13*0 20 48 2 13*0 20 48 2 13*0 20 48 2 13*0 20 48 2 13*0 20 48 2 13*0 20 48 2
  //   13*0 20 48 2 13*0 20 48 2 13*0 20 48 2 13*0 20 48 2 13*0 20 48 2 13*0 20 48 2 13*0 20 48 2 13*0 20
  //   48 2 13*0 20 48 2 13*0 20 48 2 13*0 20 48 2 13*0 20 48 2 13*0 20 48 2 13*0 20 48 2 13*0 20 48 2 13*0
  //   20 48 2 13*0 20 48 2 13*0 20 48 2 13*0 20 48 2 13*0 20 48 2 13*0 20 48 2 13*0 20 48 2 13*0 20 48 2
  //   13*0 20 48 2 13*0 20 48 2 13*0 20 48 2 13*0 20 48 2 13*0 20 48 2 13*0 20 48 2 13*0 20 48 2 13*0 20
  //   48 2 13*0 20 48 2 13*0 20 48 2 13*0 20 48 2 13*0 20 48 2 13*0 20 48 2 13*0 20 48 2 13*0 20 48 2 13*0
  //   20 48 2 13*0 20 48 2 13*0 20 48 2 13*0 20 48 2 13*0 20 48 2 13*0 20 48 2 13*0 20 48 2 13*0 20 48 2
  //   13*0 20 48 2 13*0 20 48 2 13*0 20 48 2 13*0 20 48 2 13*0 20 48 2 13*0 20 48 2 13*0 20 48 2 13*0 20
  //   48 2 13*0 20 48 2 13*0 20 48 2 13*0 20 48 2 13*0 20 48 2 13*0 20 48 2 13*0 20 48 2 13*0 20 48 2 13*0
  //   20 48 2 13*0 20 48 2 13*0 20 48 2 13*0 20 48 2 13*0 20 48 2 13*0 20 48 2 13*0 20 48 2 13*0 20 48 2
  //   13*0 20 48 2 13*0 20 48 2 13*0 20 48 2 13*0 20 48 2 13*0 20 48 2 13*0 20 48 2 13*0 20 48 2 13*0 20
  //   48 2 13*0 20 48 2 13*0 20 48 2 13*0 20 48 2 13*0 20 48 2 13*0 20 48 2 13*0 20 48 2 13*0 20 48 2 13*0
  //   20 48 2 13*0 20 48 2 13*0 20 48 2 13*0 20 48 2 13*0 20 48 2 13*0 20 48 2 13*0 20 48 2 13*0 20 48 2
  //   13*0 20 48 2 13*0 20 48 2 13*0 20 48 2 13*0 20 48 2 13*0 20 48 2 13*0 20 48 2 13*0 20 48 2 13*0 20
  //   48 2 13*0 20 48 2 13*0 20 48 2 13*0 20 48 2 13*0 20 48 2 13*0 20 48 2 13*0 20 48 2 13*0 20 48 2 13*0
  //   20 48 2 13*0 20 48 2 13*0 20 48 2 13*0 20 48 2 13*0 20 48 2 13*0 20 48 2 13*0 20 48 2 13*0 20 48 2
  //   13*0 20 48 2 13*0 20 48 2 13*0 20 48 2 13*0 20 48 2 13*0 20 48 2 13*0 20 48 2 13*0 20 48 2 13*0 20
  //   48 2 13*0 20 48 2 13*0 20 48 2 13*0 20 48 2 13*0 20 48 2 13*0 20 48 2 13*0 20 48 2 13*0 20 48 2 13*0
  //   20 48 2 13*0 20 48 2 13*0 20 48 2 13*0 20 48 2 13*0 20 48 2 13*0 20 48 2 13*0 20 48 2 13*0 20 48 2
  //   13*0 20 48 2 13*0 20 48 2 13*0 20 48 2 13*0 20 48 2 13*0 20 48 2 13*0 20 48 2 13*0 20 48 2 13*0 20
  //   48 2 13*0 20 48 2 13*0 20 48 2 13*0 20 48 2 13*0 20 48 2 13*0 20 48 2 13*0 20 48 2 13*0 20 48 2 13*0
  //   20 48 2 13*0 20 48 2 13*0 20 48 2 13*0 20 48 2 13*0 20 48 2 13*0 20 48 2 13*0 20 48 2 20 48 1 10*0
  //   20 48 2 20 48 20 4c 1 8*0 20 48 2 20 48 20 4c 20 4c 1 6*0 20 48 2 20 48 20 4c 10 8*0 20 48 2 20 48
  //   20 4c 20 4c 10 6*0 20 48 2 20 48 0 1 9*0 20 48 2 20 48 20 4c 0 1 7*0 20 48 2 20 48 0 1 9*0 20 48 2
  //   20 48 20 4c 0 1 7*0 20 48 2 20 48 0 4 9*0 20 48 2 20 48 0 4 9*0 20 48 2 13*0 20 48 2 13*0 20 48 2 20
  //   48 0 4 9*0 20 48 2 13*0 20 48 2 20 48 0 4 9*0 20 48 2 13*0 20 48 2 13*0 20 48 2 13*0 20 48 2 20 48
  //   10 10*0 20 48 2 0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
  //   contents of microcode_b (hex, n*v repeats v):
  //   0 0 10 15*0 10 0 0 10 12*0 10 0 0 10 10 11*0 10 0 0 10 10 11*0 10 0 0 10 10 11*0 10 0 0 10 10 11*0
  //   10 0 0 90 20 11*0 10 0 0 10 10 80 20 9*0 10 0 0 90 60 11*0 10 0 0 10 10 80 60 9*0 10 0 0 90 18 4
  //   10*0 10 10 10 13*0 10 0 0 90 18 4 10*0 10 10 10 13*0 10 0 0 90 18 4 10*0 10 10 10 13*0 10 0 0 90 18
  //   4 10*0 10 1 14*0 10 3 14*0 10 2 14*0 10 0 0 3 12*0 10 2 14*0 10 0 0 3 0 0 3 0 0 90 18 4 4*0 10 2 0 0
  //   6 0 0 8 10 10 6*0 10 15*0 10 15*0 10 15*0 10 15*0 10 15*0 10 15*0 10 15*0 10 15*0 10 15*0 10 15*0 10
  //   15*0 10 15*0 10 15*0 10 15*0 10 15*0 10 15*0 10 15*0 10 15*0 10 15*0 10 15*0 10 15*0 10 15*0 10 15*0
  //   10 15*0 10 15*0 10 15*0 10 15*0 10 15*0 10 15*0 10 15*0 10 15*0 10 15*0 10 15*0 10 15*0 10 15*0 10
  //   15*0 10 15*0 10 15*0 10 15*0 10 15*0 10 15*0 10 15*0 10 15*0 10 15*0 10 15*0 10 15*0 10 15*0 10 15*0
  //   10 15*0 10 15*0 10 15*0 10 15*0 10 15*0 10 15*0 10 15*0 10 15*0 10 15*0 10 15*0 10 15*0 10 15*0 10
  //   15*0 10 15*0 10 15*0 10 15*0 10 15*0 10 15*0 10 15*0 10 15*0 10 15*0 10 15*0 10 15*0 10 15*0 10 15*0
  //   10 15*0 10 15*0 10 15*0 10 15*0 10 15*0 10 15*0 10 15*0 10 15*0 10 15*0 10 15*0 10 15*0 10 15*0 10
  //   15*0 10 15*0 10 15*0 10 15*0 10 15*0 10 15*0 10 15*0 10 15*0 10 15*0 10 15*0 10 15*0 10 15*0 10 15*0
  //   10 15*0 10 15*0 10 15*0 10 15*0 10 15*0 10 15*0 10 15*0 10 15*0 10 15*0 10 15*0 10 15*0 10 15*0 10
  //   15*0 10 15*0 10 15*0 10 15*0 10 15*0 10 15*0 10 15*0 10 15*0 10 15*0 10 15*0 10 15*0 10 15*0 10 15*0
  //   10 15*0 10 15*0 10 15*0 10 15*0 10 15*0 10 15*0 10 15*0 10 15*0 10 15*0 10 15*0 10 15*0 10 15*0 10
  //   15*0 10 15*0 10 15*0 10 15*0 10 15*0 10 15*0 10 15*0 10 15*0 10 15*0 10 15*0 10 15*0 10 15*0 10 15*0
  //   10 15*0 10 15*0 10 15*0 10 15*0 10 15*0 10 15*0 10 15*0 10 15*0 10 15*0 10 15*0 10 15*0 10 15*0 10
  //   15*0 10 15*0 10 15*0 10 15*0 10 15*0 10 15*0 10 15*0 10 15*0 10 15*0 10 15*0 10 15*0 10 15*0 10 15*0
  //   10 15*0 10 15*0 10 15*0 10 15*0 10 15*0 10 15*0 10 15*0 10 15*0 10 15*0 10 15*0 10 15*0 10 15*0 10
  //   15*0 10 15*0 10 15*0 10 15*0 10 15*0 10 15*0 10 15*0 10 15*0 10 15*0 10 15*0 10 15*0 10 15*0 10 15*0
  //   10 15*0 10 15*0 10 15*0 10 15*0 10 15*0 10 15*0 10 15*0 10 15*0 10 15*0 10 15*0 10 15*0 10 15*0 10
  //   15*0 10 15*0 10 15*0 10 15*0 10 15*0 10 15*0 10 15*0 10 15*0 10 15*0 10 15*0 10 15*0 10 15*0 10 15*0
  //   10 15*0 10 15*0 10 15*0 10 15*0 10 15*0 10 15*0 10 15*0 10 15*0 10 15*0 10 15*0 10 0 0 10 12*0 10 0
  //   0 10 10 11*0 10 0 0 10 10 11*0 10 0 0 10 10 11*0 10 0 0 10 10 11*0 10 0 0 90 20 11*0 10 0 0 10 10 80
  //   20 9*0 10 0 0 90 60 11*0 10 0 0 10 10 80 60 9*0 10 0 0 90 18 4 10*0 10 0 0 90 18 4 10*0 10 10 10
  //   13*0 10 10 10 13*0 10 0 0 90 18 4 10*0 10 10 10 13*0 10 0 0 90 18 4 10*0 10 1 14*0 10 3 14*0 10 2
  //   14*0 10 0 0 3 12*0 10 2 14*0 10 0 0 3 0 0 3 0 0 90 18 4 4*0 10 2 0 0 6 0 0 8 10 10 6*0 10 15*0 10
  //   15*0 10 15*0 10 15*0 10 15*0 10 15*0 10 15*0 10 15*0 10 15*0 10 15*0 10 15*0 10 15*0 10 15*0 10 15*0
  //   10 15*0 10 15*0 10 15*0 10 15*0 10 15*0 10 15*0 10 15*0 10 15*0 10 15*0 10 15*0 10 15*0 10 15*0 10
  //   15*0 10 15*0 10 15*0 10 15*0 10 15*0 10 15*0 10 15*0 10 15*0 10 15*0 10 15*0 10 15*0 10 15*0 10 15*0
  //   10 15*0 10 15*0 10 15*0 10 15*0 10 15*0 10 15*0 10 15*0 10 15*0 10 15*0 10 15*0 10 15*0 10 15*0 10
  //   15*0 10 15*0 10 15*0 10 15*0 10 15*0 10 15*0 10 15*0 10 15*0 10 15*0 10 15*0 10 15*0 10 15*0 10 15*0
  //   10 15*0 10 15*0 10 15*0 10 15*0 10 15*0 10 15*0 10 15*0 10 15*0 10 15*0 10 15*0 10 15*0 10 15*0 10
  //   15*0 10 15*0 10 15*0 10 15*0 10 15*0 10 15*0 10 15*0 10 15*0 10 15*0 10 15*0 10 15*0 10 15*0 10 15*0
  //   10 15*0 10 15*0 10 15*0 10 15*0 10 15*0 10 15*0 10 15*0 10 15*0 10 15*0 10 15*0 10 15*0 10 15*0 10
  //   15*0 10 15*0 10 15*0 10 15*0 10 15*0 10 15*0 10 15*0 10 15*0 10 15*0 10 15*0 10 15*0 10 15*0 10 15*0
  //   10 15*0 10 15*0 10 15*0 10 15*0 10 15*0 10 15*0 10 15*0 10 15*0 10 15*0 10 15*0 10 15*0 10 15*0 10
  //   15*0 10 15*0 10 15*0 10 15*0 10 15*0 10 15*0 10 15*0 10 15*0 10 15*0 10 15*0 10 15*0 10 15*0 10 15*0
  //   10 15*0 10 15*0 10 15*0 10 15*0 10 15*0 10 15*0 10 15*0 10 15*0 10 15*0 10 15*0 10 15*0 10 15*0 10
  //   15*0 10 15*0 10 15*0 10 15*0 10 15*0 10 15*0 10 15*0 10 15*0 10 15*0 10 15*0 10 15*0 10 15*0 10 15*0
  //   10 15*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
  //   contents of microcode_c (hex, n*v repeats v):
  //   6 5 11 13*0 6 5 1 6 5 11 10*0 6 5 1 6 5 1 1 11 8*0 6 5 1 6 5 4*1 11 6*0 6 5 1 6 5 1 1 12 8*0 6 5 1 6
  //   5 4*1 12 6*0 6 5 1 6 5 1 14 9*0 6 5 1 6 5 1 1 1 14 7*0 6 5 1 6 5 1 14 9*0 6 5 1 6 5 1 1 1 14 7*0 6 5
  //   1 6 5 1 1 13 8*0 6 5 1 0 10 11*0 6 5 1 6 5 1 1 13 8*0 6 5 1 0 10 11*0 6 5 1 6 5 1 1 13 8*0 6 5 1 0
  //   10 11*0 6 5 1 6 5 1 1 13 8*0 6 5 1 10 12*0 6 5 1 10 12*0 6 5 1 10 12*0 6 5 1 8 7 12 10*0 6 5 1 0 8 7
  //   11 9*0 6 5 1 8 7 5 8 7 6 6 5 1 1 13 0 0 6 5 1 0 8 7 1 8 7 1 0 10 4*0 6 5 1 10 12*0 6 5 11 13*0 6 5
  //   11 13*0 6 5 11 13*0 6 5 11 13*0 6 5 11 13*0 6 5 11 13*0 6 5 11 13*0 6 5 11 13*0 6 5 11 13*0 6 5 11
  //   13*0 6 5 11 13*0 6 5 11 13*0 6 5 11 13*0 6 5 11 13*0 6 5 11 13*0 6 5 11 13*0 6 5 11 13*0 6 5 11 13*0
  //   6 5 11 13*0 6 5 11 13*0 6 5 11 13*0 6 5 11 13*0 6 5 11 13*0 6 5 11 13*0 6 5 11 13*0 6 5 11 13*0 6 5
  //   11 13*0 6 5 11 13*0 6 5 11 13*0 6 5 11 13*0 6 5 11 13*0 6 5 11 13*0 6 5 11 13*0 6 5 11 13*0 6 5 11
  //   13*0 6 5 11 13*0 6 5 11 13*0 6 5 11 13*0 6 5 11 13*0 6 5 11 13*0 6 5 11 13*0 6 5 11 13*0 6 5 11 13*0
  //   6 5 11 13*0 6 5 11 13*0 6 5 11 13*0 6 5 11 13*0 6 5 11 13*0 6 5 11 13*0 6 5 11 13*0 6 5 11 13*0 6 5
  //   11 13*0 6 5 11 13*0 6 5 11 13*0 6 5 11 13*0 6 5 11 13*0 6 5 11 13*0 6 5 11 13*0 6 5 11 13*0 6 5 11
  //   13*0 6 5 11 13*0 6 5 11 13*0 6 5 11 13*0 6 5 11 13*0 6 5 11 13*0 6 5 11 13*0 6 5 11 13*0 6 5 11 13*0
  //   6 5 11 13*0 6 5 11 13*0 6 5 11 13*0 6 5 11 13*0 6 5 11 13*0 6 5 11 13*0 6 5 11 13*0 6 5 11 13*0 6 5
  //   11 13*0 6 5 11 13*0 6 5 11 13*0 6 5 11 13*0 6 5 11 13*0 6 5 11 13*0 6 5 11 13*0 6 5 11 13*0 6 5 11
  //   13*0 6 5 11 13*0 6 5 11 13*0 6 5 11 13*0 6 5 11 13*0 6 5 11 13*0 6 5 11 13*0 6 5 11 13*0 6 5 11 13*0
  //   6 5 11 13*0 6 5 11 13*0 6 5 11 13*0 6 5 11 13*0 6 5 11 13*0 6 5 11 13*0 6 5 11 13*0 6 5 11 13*0 6 5
  //   11 13*0 6 5 11 13*0 6 5 11 13*0 6 5 11 13*0 6 5 11 13*0 6 5 11 13*0 6 5 11 13*0 6 5 11 13*0 6 5 11
  //   13*0 6 5 11 13*0 6 5 11 13*0 6 5 11 13*0 6 5 11 13*0 6 5 11 13*0 6 5 11 13*0 6 5 11 13*0 6 5 11 13*0
  //   6 5 11 13*0 6 5 11 13*0 6 5 11 13*0 6 5 11 13*0 6 5 11 13*0 6 5 11 13*0 6 5 11 13*0 6 5 11 13*0 6 5
  //   11 13*0 6 5 11 13*0 6 5 11 13*0 6 5 11 13*0 6 5 11 13*0 6 5 11 13*0 6 5 11 13*0 6 5 11 13*0 6 5 11
  //   13*0 6 5 11 13*0 6 5 11 13*0 6 5 11 13*0 6 5 11 13*0 6 5 11 13*0 6 5 11 13*0 6 5 11 13*0 6 5 11 13*0
  //   6 5 11 13*0 6 5 11 13*0 6 5 11 13*0 6 5 11 13*0 6 5 11 13*0 6 5 11 13*0 6 5 11 13*0 6 5 11 13*0 6 5
  //   11 13*0 6 5 11 13*0 6 5 11 13*0 6 5 11 13*0 6 5 11 13*0 6 5 11 13*0 6 5 11 13*0 6 5 11 13*0 6 5 11
  //   13*0 6 5 11 13*0 6 5 11 13*0 6 5 11 13*0 6 5 11 13*0 6 5 11 13*0 6 5 11 13*0 6 5 11 13*0 6 5 11 13*0
  //   6 5 11 13*0 6 5 11 13*0 6 5 11 13*0 6 5 11 13*0 6 5 11 13*0 6 5 11 13*0 6 5 11 13*0 6 5 11 13*0 6 5
  //   11 13*0 6 5 11 13*0 6 5 11 13*0 6 5 11 13*0 6 5 11 13*0 6 5 11 13*0 6 5 11 13*0 6 5 11 13*0 6 5 11
  //   13*0 6 5 11 13*0 6 5 11 13*0 6 5 11 13*0 6 5 11 13*0 6 5 11 13*0 6 5 11 13*0 6 5 11 13*0 6 5 11 13*0
  //   6 5 11 13*0 6 5 11 13*0 6 5 11 13*0 6 5 11 13*0 6 5 11 13*0 6 5 11 13*0 6 5 11 13*0 6 5 11 13*0 6 5
  //   11 13*0 6 5 11 13*0 6 5 11 13*0 6 5 11 13*0 6 5 11 13*0 6 5 11 13*0 6 5 11 13*0 6 5 11 13*0 6 5 11
  //   13*0 6 5 11 13*0 6 5 11 13*0 6 5 11 13*0 6 5 11 13*0 6 5 11 13*0 6 5 11 13*0 6 5 11 13*0 6 5 11 13*0
  //   6 5 11 13*0 6 5 11 13*0 6 5 11 13*0 6 5 11 13*0 6 5 11 13*0 6 5 11 13*0 6 5 11 13*0 6 5 11 13*0 6 5
  //   11 13*0 6 5 11 13*0 6 5 11 13*0 6 5 11 13*0 6 5 11 13*0 6 5 11 13*0 6 5 1 6 5 11 10*0 6 5 1 6 5 1 1
  //   11 8*0 6 5 1 6 5 4*1 11 6*0 6 5 1 6 5 1 1 12 8*0 6 5 1 6 5 4*1 12 6*0 6 5 1 6 5 1 14 9*0 6 5 1 6 5 1
  //   1 1 14 7*0 6 5 1 6 5 1 14 9*0 6 5 1 6 5 1 1 1 14 7*0 6 5 1 6 5 1 1 13 8*0 6 5 1 6 5 1 1 13 8*0 6 5 1
  //   0 10 11*0 6 5 1 0 10 11*0 6 5 1 6 5 1 1 13 8*0 6 5 1 0 10 11*0 6 5 1 6 5 1 1 13 8*0 6 5 1 10 12*0 6
  //   5 1 10 12*0 6 5 1 10 12*0 6 5 1 8 7 12 10*0 6 5 1 0 8 7 11 9*0 6 5 1 8 7 5 8 7 6 6 5 1 1 13 0 0 6 5
  //   1 0 8 7 1 8 7 1 0 10 4*0 6 5 1 10 12*0 6 5 11 13*0 6 5 11 13*0 6 5 11 13*0 6 5 11 13*0 6 5 11 13*0 6
  //   5 11 13*0 6 5 11 13*0 6 5 11 13*0 6 5 11 13*0 6 5 11 13*0 6 5 11 13*0 6 5 11 13*0 6 5 11 13*0 6 5 11
  //   13*0 6 5 11 13*0 6 5 11 13*0 6 5 11 13*0 6 5 11 13*0 6 5 11 13*0 6 5 11 13*0 6 5 11 13*0 6 5 11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
endmodule

module stack_pointer (
  input  CLK,
  input  [1:0] MODE,
  input  HO,
  input  LO,
  output [7:0] out_bus
);

  wire and_1_out, counter_2_carry, decoder_1_out0, decoder_1_out1, decoder_1_out2, decoder_1_out3, or_1_out,
       or_2_out, or_3_out;
  wire [7:0] counter_1_q, counter_2_q;

  // NoConnect on decoder_1_out0
  Decoder #(.enable("false"), .select(2)) decoder_1 (
    .out0(decoder_1_out0), .out1(decoder_1_out1), .out2(decoder_1_out2), .out3(decoder_1_out3), .sel(MODE));
  LED DEC (.in(decoder_1_out3));
  LED LOAD (.in(decoder_1_out1));
  LED INC (.in(decoder_1_out2));
  or or_1 (or_1_out, decoder_1_out2, decoder_1_out3);
  and and_1 (and_1_out, or_1_out, counter_2_carry);
  or or_2 (or_2_out, decoder_1_out1, decoder_1_out2, decoder_1_out3);
  or or_3 (or_3_out, decoder_1_out1, and_1_out);
  Counter counter_1 (
    .load(decoder_1_out1), .up(decoder_1_out2), .count(or_3_out), .clk(CLK), .D({8{1'b1}}), .Q(counter_1_q));  // open: clr, carry
  Counter counter_2 (
    .load(decoder_1_out1), .up(decoder_1_out2), .count(or_2_out), .clk(CLK), .D({8{1'b1}}),
    .carry(counter_2_carry), .Q(counter_2_q));  // open: clr
  assign out_bus = HO ? counter_1_q : 8'bz;  // Controlled_Buffer controlled_buffer_1
  assign out_bus = LO ? counter_2_q : 8'bz;  // Controlled_Buffer controlled_buffer_2
endmodule

module program_counter (
  input  CLK,
  input  CE,
  input  HI,
  input  HO,
  input  LI,
  input  LO,
  input  [7:0] bus_in,
  output [7:0] bus_out
);

  wire and_1_out, CL_carry, or_1_out, or_2_out;
  wire [7:0] CH_q, CL_q;

  and and_1 (and_1_out, CE, CL_carry);
  or or_1 (or_1_out, LI, CE);
  or or_2 (or_2_out, HI, and_1_out);
  Counter CH (.load(HI), .count(or_2_out), .clk(CLK), .D(bus_in), .Q(CH_q));  // open: clr, up, carry
  Counter CL (.load(LI), .count(or_1_out), .clk(CLK), .D(bus_in), .carry(CL_carry), .Q(CL_q));  // open: clr, up
  assign bus_out = HO ? CH_q : 8'bz;  // Controlled_Buffer controlled_buffer_1
  assign bus_out = LO ? CL_q : 8'bz;  // Controlled_Buffer controlled_buffer_2
endmodule

module mar (
  input  CLK,
  input  HI,
  input  LI,
  input  [7:0] bus_in,
  input  U,
  output [15:0] addr
);

  wire [7:0] MARH_q, MARL_q;

  Register MARH (.D(bus_in), .en(HI), .clk(CLK), .Q(MARH_q));  // open: clr
  Register MARL (.D(bus_in), .en(LI), .clk(CLK), .Q(MARL_q));  // open: clr
  Register #(.trigger("high"), .width(16)) register_1 (.D({MARH_q, MARL_q}), .en(U), .clk(CLK), .Q(addr));  // open: clr
endmodule
